# Fritzing sketch finalproject (saved by Fritzing 0.9.3b)
breadboards: 1

parts:
  U1 = mystery part, 7 pins [chip_label=?]
  V1 = DC Power [voltage=5]
  S1 = Pushbutton [package=THT]
  S2 = Pushbutton [package=THT]
  S3 = Pushbutton [package=THT]
  S4 = Pushbutton [package=THT]
  L1 = Solenoid
  L2 = Solenoid
  L3 = Solenoid
  L4 = Solenoid
  S5 = Pushbutton [package=THT]
  S6 = Pushbutton [package=THT]
  S7 = Pushbutton [package=THT]
  S8 = Pushbutton [package=THT]
  L5 = Solenoid
  R2 = Resistor [tolerance=±5% resistance=10k package=THT]
  R3 = Resistor [tolerance=±5% resistance=10k package=THT]
  R4 = Resistor [tolerance=±5% resistance=10k package=THT]
  R5 = Resistor [tolerance=±5% resistance=10k package=THT]
  Q1 = PNP-Transistor [package="TO92 [THT]"]
  Q2 = PNP-Transistor [package="TO92 [THT]"]
  Q3 = PNP-Transistor [package="TO92 [THT]"]
  Q4 = PNP-Transistor [package="TO92 [THT]"]
  Q5 = PNP-Transistor [package="TO92 [THT]"]
  R6 = Resistor [tolerance=±5% resistance=10k package=THT]
  L6 = Solenoid
  L7 = Solenoid
  L8 = Solenoid
  L9 = Solenoid

nets:
  N1: U1.pin1, S5.leg0, S6.leg0, S7.leg0, S8.leg0
  N2: U1.pin2, U1.pin3, U1.pin4, U1.pin5, U1.pin7, V1.V-, L1.pin1, L2.pin1, L3.pin1, L4.pin1, R2.Pin_1, R3.Pin_1, R4.Pin_1, R5.Pin_1, Q1.E, Q2.E, Q3.E, Q4.E, Q5.E
  N3: U1.pin6, Q5.B, R6.Pin_0
  N4: V1.V+, S1.leg0, S2.leg0, S3.leg0, S4.leg0, L5.pin1, L6.pin1, L7.pin1, L8.pin1, L9.pin1
  N5: S5.leg1, R3.Pin_0, Q2.B
  N6: S6.leg1, R4.Pin_0, Q1.B
  N7: S7.leg1, R5.Pin_0, Q3.B
  N8: S8.leg1, R2.Pin_0, Q4.B
  N9: L5.pin2, Q5.C
  N10: Q1.C, L8.pin2
  N11: Q2.C, L9.pin2
  N12: Q3.C, L7.pin2
  N13: Q4.C, L6.pin2
